# Fritzing sketch Basic_Test_NeoPixel_1 (saved by Fritzing 0.9.3b)
breadboards: 1

parts:
  U1 = lolin
  NEOPIXEL1 = Neopixel Strip -- White (60/m) [part_number=1138]

nets:
  N1: U1.connector14, NEOPIXEL1.+5V
  N2: U1.connector15, NEOPIXEL1.GND
  N3: U1.connector19, NEOPIXEL1.DO

custom parts:
  Neopixel Strip -- White (60/m): Neopixel Strip, White, 60 pixels per meter.
